# Fritzing sketch ledButton (saved by Fritzing 0.9.3b)
breadboards: 1

parts:
  Bauteil1 = Adafruit T-Cobbler Plus [part_number="Adafruit #1989 and #2028"]  # not connected
  Button = Pushbutton [package="[THT]"]
  R1 = Resistor [tolerance=±5% resistance=1k package="0402 [SMD]"]
  LED1 = LED - 3mm [color="Red (633nm)" package="3 mm [THT]"]
  R2 = Resistor [tolerance=±5% resistance=1k package=THT]

nets:
  N1: Button.Pin_1, Button.Pin_2
  N2: Button.Pin_3, Button.Pin_4, R1.Pin_1
  N3: R1.Pin_0, LED1.anode
  N4: LED1.cathode, R2.Pin_0

custom parts:
  Adafruit T-Cobbler Plus: The Raspberry Pi has landed on the Maker World like a 40-GPIO pinned, quad-USB ported, credit card sized bomb of DIY joy. And while you can use most of our great Model B accessories by hooking up our downgrade cable, its probably a good time to upgrade your set up and accessorize using all of the 40 pins. That's why we now carry the Assembled Adafruit Pi T-Cobbler Plus - Breakout + Cable for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
